// Logisim project ALUProjectFinal.circ as structural Verilog: 3 circuits, main circuit main
module main (
  input  [7:0] A,
  input  [7:0] B,
  input  [3:0] Opcode,
  output [7:0] ADD_OUT,
  output [7:0] AND_OUT,
  output [7:0] INC_OUT,
  output [7:0] OR_OUT,
  output [7:0] Results,
  output [7:0] DEC_OUT,
  output [7:0] XOR_OUT,
  output [7:0] NOT_OUT,
  output LT,
  output EQ,
  output GT,
  output [7:0] Shift_left,
  output [7:0] Shift_right
);

  Adder adder_1 (.a(A), .b(B), .out(ADD_OUT));  // open: cin, cout
  Adder adder_2 (.a(A), .b(8'h1), .out(INC_OUT));  // open: cin, cout
  Adder adder_3 (.a(A), .b({8{1'b1}}), .out(DEC_OUT));  // open: cin, cout
  Comparator comparator_1 (.a(A), .b(B), .gt(GT), .eq(EQ), .lt(LT));
  assign NOT_OUT = ~A;  // NOT_Gate not_1, 8 bits wide
  Shifter shifter_1 (.in(A), .\dist (3'b001), .out(Shift_left));
  Shifter #(.shift("lr")) shifter_2 (.in(A), .\dist (3'b001), .out(Shift_right));
  assign AND_OUT = A & B;  // AND_Gate and_1, 8 bits wide
  assign OR_OUT = A | B;  // OR_Gate or_1, 8 bits wide
  assign XOR_OUT = A ^ B;  // XOR_Gate xor_1, 8 bits wide
  Multiplexer #(.select(4), .width(8)) multiplexer_1 (
    .in0(ADD_OUT), .in1(INC_OUT), .in2(DEC_OUT), .in3(AND_OUT), .in4(OR_OUT), .in5(XOR_OUT), .in6(NOT_OUT),
    .in7(Shift_left), .in8(Shift_right), .out(Results), .sel(Opcode));  // open: in9, in10, in11, in12, in13, in14, in15
endmodule

module ALU8 (
  input  [7:0] A,
  input  [7:0] B,
  input  [3:0] Opcode,
  output [7:0] ADD_OUT,
  output [7:0] AND_OUT,
  output [7:0] INC_OUT,
  output [7:0] OR_OUT,
  output [7:0] Results,
  output [7:0] DEC_OUT,
  output [7:0] XOR_OUT,
  output [7:0] NOT_OUT,
  output LT,
  output EQ,
  output GT,
  output [7:0] Shift_left,
  output [7:0] Shift_right
);

  Adder adder_1 (.a(A), .b(B), .out(ADD_OUT));  // open: cin, cout
  Adder adder_2 (.a(A), .b(8'h1), .out(INC_OUT));  // open: cin, cout
  Adder adder_3 (.a(A), .b({8{1'b1}}), .out(DEC_OUT));  // open: cin, cout
  Comparator comparator_1 (.a(A), .b(B), .gt(GT), .eq(EQ), .lt(LT));
  assign NOT_OUT = ~A;  // NOT_Gate not_1, 8 bits wide
  Shifter shifter_1 (.in(A), .\dist (3'b001), .out(Shift_left));
  Shifter #(.shift("lr")) shifter_2 (.in(A), .\dist (3'b001), .out(Shift_right));
  assign AND_OUT = A & B;  // AND_Gate and_1, 8 bits wide
  assign OR_OUT = A | B;  // OR_Gate or_1, 8 bits wide
  assign XOR_OUT = A ^ B;  // XOR_Gate xor_1, 8 bits wide
  Multiplexer #(.select(4), .width(8)) multiplexer_1 (
    .in0(ADD_OUT), .in1(INC_OUT), .in2(DEC_OUT), .in3(AND_OUT), .in4(OR_OUT), .in5(XOR_OUT), .in6(NOT_OUT),
    .in7(Shift_left), .in8(Shift_right), .out(Results), .sel(Opcode));  // open: in9, in10, in11, in12, in13, in14, in15
endmodule

module ControlUnit (
);

  wire alu8_1_eq, alu8_1_gt, alu8_1_lt, clock_1_out;
  wire [2:0] counter_1_q;
  wire [3:0] Control_data, register_1_q;
  wire [7:0] A_q, alu8_1_add_out, alu8_1_and_out, alu8_1_dec_out, alu8_1_inc_out, alu8_1_not_out,
       alu8_1_or_out, alu8_1_results, alu8_1_shift_left, alu8_1_shift_right, alu8_1_xor_out, B_q, DATA_data;
  wire [7:4] Control_data_2;

  ROM #(.addrWidth(3)) DATA (.addr(counter_1_q), .data(DATA_data));
  Clock clock_1 (.out(clock_1_out));
  Register A (.D(DATA_data), .en(Control_data_2[4]), .Q(A_q), .clk(clock_1_out));  // open: clr
  Register B (.D(DATA_data), .en(Control_data_2[5]), .Q(B_q), .clk(clock_1_out));  // open: clr
  ROM #(.addrWidth(3)) Control (.addr(counter_1_q), .data({Control_data_2, Control_data}));
  Register #(.width(4)) register_1 (
    .D(Control_data), .en(Control_data_2[6]), .Q(register_1_q), .clk(clock_1_out));  // open: clr
  Counter #(.max('h7), .width(3)) counter_1 (
    .Q(counter_1_q), .clk(clock_1_out));  // open: load, D, count, carry, up, clr
  // Probe on alu8_1_add_out
  ALU8 alu8_1 (
    .A(A_q), .B(B_q), .Opcode(register_1_q), .ADD_OUT(alu8_1_add_out), .AND_OUT(alu8_1_and_out),
    .INC_OUT(alu8_1_inc_out), .OR_OUT(alu8_1_or_out), .Results(alu8_1_results), .DEC_OUT(alu8_1_dec_out),
    .XOR_OUT(alu8_1_xor_out), .NOT_OUT(alu8_1_not_out), .LT(alu8_1_lt), .EQ(alu8_1_eq), .GT(alu8_1_gt),
    .Shift_left(alu8_1_shift_left), .Shift_right(alu8_1_shift_right));
  // Probe on alu8_1_and_out
  // Probe on alu8_1_inc_out
  // Probe on alu8_1_or_out
  // Probe on alu8_1_results
  // Probe on alu8_1_dec_out
  // Probe on alu8_1_xor_out
  // Probe on alu8_1_not_out
  // Probe on alu8_1_lt
  // Probe on alu8_1_eq
  // Probe on alu8_1_gt
  // Probe on alu8_1_shift_left
  // Probe on alu8_1_shift_right

  // Notes on the sheet:
  //   contents of DATA (hex, n*v repeats v):
  //   3 5 0 ff 0 80
  //   Data
  //   contents of Control (hex, n*v repeats v):
  //   10 20 41 0 42 48
  //   Control
endmodule
